// Logisim project alu.circ as structural Verilog: 13 circuits, main circuit alu
module alu (
  input  [31:0] A,
  input  [31:0] B,
  input  [3:0] ALUSel,
  output [31:0] Result
);

  wire res;
  wire [31:0] add0, and1, not4, or2, sll6, sra5, sub8, xor3;

  add32 add32_1 (.in_1(A), .in_2(B), .Cin(1'b0), .out_4(add0));  // open: Cout
  assign and1 = A & B;  // AND_Gate and_1, 32 bits wide
  assign or2 = A | B;  // OR_Gate or_1, 32 bits wide
  assign xor3 = A ^ B;  // XOR_Gate xor_1, 32 bits wide
  assign not4 = ~A;  // NOT_Gate not_1, 32 bits wide
  sra32 sra32_1 (.in_1(1'b1), .in_2(A), .out_3(sra5));
  sll32 sll32_1 (.in_1(1'b1), .in_2(A), .out_3(sll6));
  slt slt_1 (.in_1(A), .in_2(B), .out_3(res));
  sub32 sub32_1 (.in_1(A), .in_2(B), .in_3(1'b1), .out_4(sub8));  // open: Cout
  Multiplexer #(.select(4), .width(32), .enable("false")) multiplexer_1 (
    .in0(add0), .in1(and1), .in2(or2), .in3(xor3), .in4(not4), .in5(sra5), .in6(sll6),
    .in7({{31{1'b0}}, res}), .in8(sub8), .out(Result), .sel(ALUSel));  // open: in9, in10, in11, in12, in13, in14, in15

  // Other names for the same wires on the sheet: slt7[0] = res

  // Notes on the sheet:
  //   INPUTS to your circuit
  //   DON'T CHANGE THE LOCATIONS OF THE INPUTS AND OUTPUTS!
  //   OUTPUT from your circuit
endmodule

module add1 (
  input  A0,
  input  B0,
  input  Cin,
  output SUM,
  output Cout
);

  wire and_1_out, and_2_out, xor_1_out;

  xor xor_1 (xor_1_out, A0, B0);
  xor xor_2 (SUM, xor_1_out, Cin);
  and and_1 (and_1_out, Cin, xor_1_out);
  and and_2 (and_2_out, A0, B0);
  or or_1 (Cout, and_1_out, and_2_out);
endmodule

module add2 (
  input  [1:0] in_1,
  input  [1:0] in_2,
  input  Cin,
  output [1:0] SUM,
  output Cout
);

  wire add1_1_cout;

  add1 add1_1 (.A0(in_1[0]), .B0(in_2[0]), .Cin(Cin), .SUM(SUM[0]), .Cout(add1_1_cout));
  add1 add1_2 (.A0(in_1[1]), .B0(in_2[1]), .Cin(add1_1_cout), .SUM(SUM[1]), .Cout(Cout));

  // Other names for the same wires on the sheet: A[1:0] = in_1; A0 = in_1[0]; A1 = in_1[1]; B[1:0] = in_2;
  //   B0 = in_2[0]; B1 = in_2[1]; s1 = SUM[0]; s2 = SUM[1]
endmodule

module add4 (
  input  [3:0] in_1,
  input  [3:0] in_2,
  input  Cin,
  output [3:0] SUM,
  output Cout
);

  wire add2_1_cout;

  add2 add2_1 (.in_1(in_1[1:0]), .in_2(in_2[1:0]), .Cin(Cin), .SUM(SUM[1:0]), .Cout(add2_1_cout));
  add2 add2_2 (.in_1(in_1[3:2]), .in_2(in_2[3:2]), .Cin(add2_1_cout), .SUM(SUM[3:2]), .Cout(Cout));

  // Other names for the same wires on the sheet: A[3:0] = in_1; A0[1:0] = in_1[1:0]; A1[1:0] = in_1[3:2];
  //   B[3:0] = in_2; B0[1:0] = in_2[1:0]; B1[1:0] = in_2[3:2]; s1[1:0] = SUM[1:0]; s2[1:0] = SUM[3:2]
endmodule

module add8 (
  input  [7:0] in_1,
  input  [7:0] in_2,
  input  Cin,
  output [7:0] SUM,
  output Cout
);

  wire add4_1_cout;

  add4 add4_1 (.in_1(in_1[3:0]), .in_2(in_2[3:0]), .Cin(Cin), .SUM(SUM[3:0]), .Cout(add4_1_cout));
  add4 add4_2 (.in_1(in_1[7:4]), .in_2(in_2[7:4]), .Cin(add4_1_cout), .SUM(SUM[7:4]), .Cout(Cout));

  // Other names for the same wires on the sheet: A[7:0] = in_1; A0[3:0] = in_1[3:0]; A1[3:0] = in_1[7:4];
  //   B[7:0] = in_2; B0[3:0] = in_2[3:0]; B1[3:0] = in_2[7:4]; s1[3:0] = SUM[3:0]; s2[3:0] = SUM[7:4]
endmodule

module add16 (
  input  [15:0] in_1,
  input  [15:0] in_2,
  input  Cin,
  output [15:0] SUM,
  output Cout
);

  wire add8_1_cout;

  add8 add8_1 (.in_1(in_1[7:0]), .in_2(in_2[7:0]), .Cin(Cin), .SUM(SUM[7:0]), .Cout(add8_1_cout));
  add8 add8_2 (.in_1(in_1[15:8]), .in_2(in_2[15:8]), .Cin(add8_1_cout), .SUM(SUM[15:8]), .Cout(Cout));

  // Other names for the same wires on the sheet: A[15:0] = in_1; A0[7:0] = in_1[7:0]; A1[7:0] = in_1[15:8];
  //   B[15:0] = in_2; B0[7:0] = in_2[7:0]; B1[7:0] = in_2[15:8]; s1[7:0] = SUM[7:0]; s2[7:0] = SUM[15:8]
endmodule

module add32 (
  input  [31:0] in_1,
  input  [31:0] in_2,
  input  Cin,
  output [31:0] out_4,
  output Cout
);

  wire add16_1_cout;

  add16 add16_1 (.in_1(in_1[15:0]), .in_2(in_2[15:0]), .Cin(Cin), .SUM(out_4[15:0]), .Cout(add16_1_cout));
  add16 add16_2 (.in_1(in_1[31:16]), .in_2(in_2[31:16]), .Cin(add16_1_cout), .SUM(out_4[31:16]), .Cout(Cout));

  // Other names for the same wires on the sheet: A[31:0] = in_1; A0[15:0] = in_1[15:0]; A1[15:0] = in_1[31:16];
  //   B[31:0] = in_2; B0[15:0] = in_2[15:0]; B1[15:0] = in_2[31:16]; s1[15:0] = out_4[15:0]; SUM[31:0] = out_4;
  //   s2[15:0] = out_4[31:16]

  // Notes on the sheet:
  //   SUM
endmodule

module sra32 (
  input  in_1,
  input  [31:0] in_2,
  output [31:0] out_3
);

  Multiplexer #(.enable("false")) multiplexer_1 (.in0(in_2[31]), .in1(in_2[31]), .out(out_3[31]), .sel(in_1));
  Multiplexer #(.enable("false")) multiplexer_2 (.in0(in_2[30]), .in1(in_2[31]), .out(out_3[30]), .sel(in_1));
  Multiplexer #(.enable("false")) multiplexer_3 (.in0(in_2[29]), .in1(in_2[30]), .out(out_3[29]), .sel(in_1));
  Multiplexer #(.enable("false")) multiplexer_4 (.in0(in_2[28]), .in1(in_2[29]), .out(out_3[28]), .sel(in_1));
  Multiplexer #(.enable("false")) multiplexer_5 (.in0(in_2[27]), .in1(in_2[28]), .out(out_3[27]), .sel(in_1));
  Multiplexer #(.enable("false")) multiplexer_6 (.in0(in_2[26]), .in1(in_2[27]), .out(out_3[26]), .sel(in_1));
  Multiplexer #(.enable("false")) multiplexer_7 (.in0(in_2[25]), .in1(in_2[26]), .out(out_3[25]), .sel(in_1));
  Multiplexer #(.enable("false")) multiplexer_8 (.in0(in_2[24]), .in1(in_2[25]), .out(out_3[24]), .sel(in_1));
  Multiplexer #(.enable("false")) multiplexer_9 (.in0(in_2[23]), .in1(in_2[24]), .out(out_3[23]), .sel(in_1));
  Multiplexer #(.enable("false")) multiplexer_10 (.in0(in_2[22]), .in1(in_2[23]), .out(out_3[22]), .sel(in_1));
  Multiplexer #(.enable("false")) multiplexer_11 (.in0(in_2[21]), .in1(in_2[22]), .out(out_3[21]), .sel(in_1));
  Multiplexer #(.enable("false")) multiplexer_12 (.in0(in_2[20]), .in1(in_2[21]), .out(out_3[20]), .sel(in_1));
  Multiplexer #(.enable("false")) multiplexer_13 (.in0(in_2[19]), .in1(in_2[20]), .out(out_3[19]), .sel(in_1));
  Multiplexer #(.enable("false")) multiplexer_14 (.in0(in_2[18]), .in1(in_2[19]), .out(out_3[18]), .sel(in_1));
  Multiplexer #(.enable("false")) multiplexer_15 (.in0(in_2[17]), .in1(in_2[18]), .out(out_3[17]), .sel(in_1));
  Multiplexer #(.enable("false")) multiplexer_16 (.in0(in_2[16]), .in1(in_2[17]), .out(out_3[16]), .sel(in_1));
  Multiplexer #(.enable("false")) multiplexer_17 (.in0(in_2[15]), .in1(in_2[16]), .out(out_3[15]), .sel(in_1));
  Multiplexer #(.enable("false")) multiplexer_18 (.in0(in_2[14]), .in1(in_2[15]), .out(out_3[14]), .sel(in_1));
  Multiplexer #(.enable("false")) multiplexer_19 (.in0(in_2[13]), .in1(in_2[14]), .out(out_3[13]), .sel(in_1));
  Multiplexer #(.enable("false")) multiplexer_20 (.in0(in_2[12]), .in1(in_2[13]), .out(out_3[12]), .sel(in_1));
  Multiplexer #(.enable("false")) multiplexer_21 (.in0(in_2[11]), .in1(in_2[12]), .out(out_3[11]), .sel(in_1));
  Multiplexer #(.enable("false")) multiplexer_22 (.in0(in_2[10]), .in1(in_2[11]), .out(out_3[10]), .sel(in_1));
  Multiplexer #(.enable("false")) multiplexer_23 (.in0(in_2[9]), .in1(in_2[10]), .out(out_3[9]), .sel(in_1));
  Multiplexer #(.enable("false")) multiplexer_24 (.in0(in_2[8]), .in1(in_2[9]), .out(out_3[8]), .sel(in_1));
  Multiplexer #(.enable("false")) multiplexer_25 (.in0(in_2[7]), .in1(in_2[8]), .out(out_3[7]), .sel(in_1));
  Multiplexer #(.enable("false")) multiplexer_26 (.in0(in_2[6]), .in1(in_2[7]), .out(out_3[6]), .sel(in_1));
  Multiplexer #(.enable("false")) multiplexer_27 (.in0(in_2[5]), .in1(in_2[6]), .out(out_3[5]), .sel(in_1));
  Multiplexer #(.enable("false")) multiplexer_28 (.in0(in_2[4]), .in1(in_2[5]), .out(out_3[4]), .sel(in_1));
  Multiplexer #(.enable("false")) multiplexer_29 (.in0(in_2[3]), .in1(in_2[4]), .out(out_3[3]), .sel(in_1));
  Multiplexer #(.enable("false")) multiplexer_30 (.in0(in_2[2]), .in1(in_2[3]), .out(out_3[2]), .sel(in_1));
  Multiplexer #(.enable("false")) multiplexer_31 (.in0(in_2[1]), .in1(in_2[2]), .out(out_3[1]), .sel(in_1));
  Multiplexer #(.enable("false")) multiplexer_32 (.in0(in_2[0]), .in1(in_2[1]), .out(out_3[0]), .sel(in_1));

  // Other names for the same wires on the sheet: A[31:0] = in_2; A0 = in_2[0]; A1 = in_2[1]; A2 = in_2[2];
  //   A3 = in_2[3]; A4 = in_2[4]; A5 = in_2[5]; A6 = in_2[6]; A7 = in_2[7]; A8 = in_2[8]; A9 = in_2[9];
  //   A10 = in_2[10]; A11 = in_2[11]; A12 = in_2[12]; A13 = in_2[13]; A14 = in_2[14]; A15 = in_2[15]; A16 = in_2[16];
  //   A17 = in_2[17]; A18 = in_2[18]; A19 = in_2[19]; A20 = in_2[20]; A21 = in_2[21]; A22 = in_2[22]; A23 = in_2[23];
  //   A24 = in_2[24]; A25 = in_2[25]; A26 = in_2[26]; A27 = in_2[27]; A28 = in_2[28]; A29 = in_2[29]; A30 = in_2[30];
  //   A31 = in_2[31]; B[31:0] = out_3; B0 = out_3[0]; B1 = out_3[1]; B2 = out_3[2]; B3 = out_3[3]; B4 = out_3[4];
  //   B5 = out_3[5]; B6 = out_3[6]; B7 = out_3[7]; B8 = out_3[8]; B9 = out_3[9]; B10 = out_3[10]; B11 = out_3[11];
  //   B12 = out_3[12]; B13 = out_3[13]; B14 = out_3[14]; B15 = out_3[15]; B16 = out_3[16]; B17 = out_3[17];
  //   B18 = out_3[18]; B19 = out_3[19]; B20 = out_3[20]; B21 = out_3[21]; B22 = out_3[22]; B23 = out_3[23];
  //   B24 = out_3[24]; B25 = out_3[25]; B26 = out_3[26]; B27 = out_3[27]; B28 = out_3[28]; B29 = out_3[29];
  //   B30 = out_3[30]; B31 = out_3[31]; s = in_1
endmodule

module sll32 (
  input  in_1,
  input  [31:0] in_2,
  output [31:0] out_3
);

  Multiplexer #(.enable("false")) multiplexer_1 (.in0(in_2[31]), .in1(in_2[30]), .out(out_3[31]), .sel(in_1));
  Multiplexer #(.enable("false")) multiplexer_2 (.in0(in_2[30]), .in1(in_2[29]), .out(out_3[30]), .sel(in_1));
  Multiplexer #(.enable("false")) multiplexer_3 (.in0(in_2[29]), .in1(in_2[28]), .out(out_3[29]), .sel(in_1));
  Multiplexer #(.enable("false")) multiplexer_4 (.in0(in_2[28]), .in1(in_2[27]), .out(out_3[28]), .sel(in_1));
  Multiplexer #(.enable("false")) multiplexer_5 (.in0(in_2[27]), .in1(in_2[26]), .out(out_3[27]), .sel(in_1));
  Multiplexer #(.enable("false")) multiplexer_6 (.in0(in_2[26]), .in1(in_2[25]), .out(out_3[26]), .sel(in_1));
  Multiplexer #(.enable("false")) multiplexer_7 (.in0(in_2[25]), .in1(in_2[24]), .out(out_3[25]), .sel(in_1));
  Multiplexer #(.enable("false")) multiplexer_8 (.in0(in_2[24]), .in1(in_2[23]), .out(out_3[24]), .sel(in_1));
  Multiplexer #(.enable("false")) multiplexer_9 (.in0(in_2[23]), .in1(in_2[22]), .out(out_3[23]), .sel(in_1));
  Multiplexer #(.enable("false")) multiplexer_10 (.in0(in_2[22]), .in1(in_2[21]), .out(out_3[22]), .sel(in_1));
  Multiplexer #(.enable("false")) multiplexer_11 (.in0(in_2[21]), .in1(in_2[20]), .out(out_3[21]), .sel(in_1));
  Multiplexer #(.enable("false")) multiplexer_12 (.in0(in_2[20]), .in1(in_2[19]), .out(out_3[20]), .sel(in_1));
  Multiplexer #(.enable("false")) multiplexer_13 (.in0(in_2[19]), .in1(in_2[18]), .out(out_3[19]), .sel(in_1));
  Multiplexer #(.enable("false")) multiplexer_14 (.in0(in_2[18]), .in1(in_2[17]), .out(out_3[18]), .sel(in_1));
  Multiplexer #(.enable("false")) multiplexer_15 (.in0(in_2[17]), .in1(in_2[16]), .out(out_3[17]), .sel(in_1));
  Multiplexer #(.enable("false")) multiplexer_16 (.in0(in_2[16]), .in1(in_2[15]), .out(out_3[16]), .sel(in_1));
  Multiplexer #(.enable("false")) multiplexer_17 (.in0(in_2[15]), .in1(in_2[14]), .out(out_3[15]), .sel(in_1));
  Multiplexer #(.enable("false")) multiplexer_18 (.in0(in_2[14]), .in1(in_2[13]), .out(out_3[14]), .sel(in_1));
  Multiplexer #(.enable("false")) multiplexer_19 (.in0(in_2[13]), .in1(in_2[12]), .out(out_3[13]), .sel(in_1));
  Multiplexer #(.enable("false")) multiplexer_20 (.in0(in_2[12]), .in1(in_2[11]), .out(out_3[12]), .sel(in_1));
  Multiplexer #(.enable("false")) multiplexer_21 (.in0(in_2[11]), .in1(in_2[10]), .out(out_3[11]), .sel(in_1));
  Multiplexer #(.enable("false")) multiplexer_22 (.in0(in_2[10]), .in1(in_2[9]), .out(out_3[10]), .sel(in_1));
  Multiplexer #(.enable("false")) multiplexer_23 (.in0(in_2[9]), .in1(in_2[8]), .out(out_3[9]), .sel(in_1));
  Multiplexer #(.enable("false")) multiplexer_24 (.in0(in_2[8]), .in1(in_2[7]), .out(out_3[8]), .sel(in_1));
  Multiplexer #(.enable("false")) multiplexer_25 (.in0(in_2[7]), .in1(in_2[6]), .out(out_3[7]), .sel(in_1));
  Multiplexer #(.enable("false")) multiplexer_26 (.in0(in_2[6]), .in1(in_2[5]), .out(out_3[6]), .sel(in_1));
  Multiplexer #(.enable("false")) multiplexer_27 (.in0(in_2[5]), .in1(in_2[4]), .out(out_3[5]), .sel(in_1));
  Multiplexer #(.enable("false")) multiplexer_28 (.in0(in_2[4]), .in1(in_2[3]), .out(out_3[4]), .sel(in_1));
  Multiplexer #(.enable("false")) multiplexer_29 (.in0(in_2[3]), .in1(in_2[2]), .out(out_3[3]), .sel(in_1));
  Multiplexer #(.enable("false")) multiplexer_30 (.in0(in_2[2]), .in1(in_2[1]), .out(out_3[2]), .sel(in_1));
  Multiplexer #(.enable("false")) multiplexer_31 (.in0(in_2[1]), .in1(in_2[0]), .out(out_3[1]), .sel(in_1));
  Multiplexer #(.enable("false")) multiplexer_32 (.in0(in_2[0]), .in1(1'b0), .out(out_3[0]), .sel(in_1));

  // Other names for the same wires on the sheet: A[31:0] = in_2; A0 = in_2[0]; A1 = in_2[1]; A2 = in_2[2];
  //   A3 = in_2[3]; A4 = in_2[4]; A5 = in_2[5]; A6 = in_2[6]; A7 = in_2[7]; A8 = in_2[8]; A9 = in_2[9];
  //   A10 = in_2[10]; A11 = in_2[11]; A12 = in_2[12]; A13 = in_2[13]; A14 = in_2[14]; A15 = in_2[15]; A16 = in_2[16];
  //   A17 = in_2[17]; A18 = in_2[18]; A19 = in_2[19]; A20 = in_2[20]; A21 = in_2[21]; A22 = in_2[22]; A23 = in_2[23];
  //   A24 = in_2[24]; A25 = in_2[25]; A26 = in_2[26]; A27 = in_2[27]; A28 = in_2[28]; A29 = in_2[29]; A30 = in_2[30];
  //   A31 = in_2[31]; B[31:0] = out_3; B0 = out_3[0]; B1 = out_3[1]; B2 = out_3[2]; B3 = out_3[3]; B4 = out_3[4];
  //   B5 = out_3[5]; B6 = out_3[6]; B7 = out_3[7]; B8 = out_3[8]; B9 = out_3[9]; B10 = out_3[10]; B11 = out_3[11];
  //   B12 = out_3[12]; B13 = out_3[13]; B14 = out_3[14]; B15 = out_3[15]; B16 = out_3[16]; B17 = out_3[17];
  //   B18 = out_3[18]; B19 = out_3[19]; B20 = out_3[20]; B21 = out_3[21]; B22 = out_3[22]; B23 = out_3[23];
  //   B24 = out_3[24]; B25 = out_3[25]; B26 = out_3[26]; B27 = out_3[27]; B28 = out_3[28]; B29 = out_3[29];
  //   B30 = out_3[30]; B31 = out_3[31]; s = in_1
endmodule

module sub32 (
  input  [31:0] in_1,
  input  [31:0] in_2,
  input  in_3,
  output [31:0] out_4,
  output Cout
);

  wire [31:0] not_1_out;

  assign not_1_out = ~in_2;  // NOT_Gate not_1, 32 bits wide
  add32 add32_1 (.in_1(in_1), .in_2(not_1_out), .Cin(in_3), .out_4(out_4), .Cout(Cout));

  // Other names for the same wires on the sheet: A[31:0] = in_1; B[31:0] = in_2; Cin = in_3; DIFF[31:0] = out_4
endmodule

module samesign (
  input  [31:0] in_1,
  input  [31:0] in_2,
  output out_3
);

  wire [30:0] SUB;

  sub32 sub32_1 (.in_1(in_1), .in_2(in_2), .in_3(1'b1), .out_4({out_3, SUB}));  // open: Cout

  // Other names for the same wires on the sheet: A[31:0] = in_1; Asign = in_1[31]; B[31:0] = in_2; Bsign = in_2[31];
  //   Ssign = out_3; SUB[31] = out_3
endmodule

module diffsign (
  input  [31:0] in_1,
  input  [31:0] in_2,
  output out_3
);


  assign out_3 = in_1[31];

  // Other names for the same wires on the sheet: A[31:0] = in_1; Asign = in_1[31]; B[31:0] = in_2
endmodule

module slt (
  input  [31:0] in_1,
  input  [31:0] in_2,
  output out_3
);

  wire diffsign_1_out_3, s, samesign_1_out_3;

  xnor xnor_1 (s, in_1[31], in_2[31]);
  diffsign diffsign_1 (.in_1(in_1), .in_2(in_2), .out_3(diffsign_1_out_3));
  samesign samesign_1 (.in_1(in_1), .in_2(in_2), .out_3(samesign_1_out_3));
  Multiplexer #(.enable("false")) multiplexer_1 (.in0(diffsign_1_out_3), .in1(samesign_1_out_3), .out(out_3), .sel(s));

  // Other names for the same wires on the sheet: A[31:0] = in_1; Asign = in_1[31]; B[31:0] = in_2; Bsign = in_2[31]
endmodule
