// Logisim project regfile.circ as structural Verilog: 3 circuits, main circuit main
module main (
  input  [4:0] rs1,
  input  [4:0] rs2,
  input  [4:0] rd,
  input  [31:0] Write_Data,
  input  RegWEn,
  input  clk,
  output [31:0] ra,
  output [31:0] sp,
  output [31:0] t0,
  output [31:0] t1,
  output [31:0] t2,
  output [31:0] s0,
  output [31:0] s1,
  output [31:0] a0,
  output [31:0] Read_Data_1,
  output [31:0] Read_Data_2
);

  wire and_1_out, and_2_out, and_3_out, and_4_out, and_5_out, and_6_out, and_7_out, and_8_out, and_9_out,
       decoder_1_out0, decoder_1_out1, decoder_1_out2, decoder_1_out5, decoder_1_out6, decoder_1_out7,
       decoder_1_out8, decoder_1_out9, decoder_1_out10;
  wire [31:0] regfilesadness_1_out_5;

  Decoder #(.select(5)) decoder_1 (
    .out0(decoder_1_out0), .out1(decoder_1_out1), .out2(decoder_1_out2), .out5(decoder_1_out5),
    .out6(decoder_1_out6), .out7(decoder_1_out7), .out8(decoder_1_out8), .out9(decoder_1_out9),
    .out10(decoder_1_out10), .sel(rd));  // open: out3, out4, out11, out12, out13, out14, out15, out16, out17, out18, out19, out20, out21, out22, out23, out24, out25, out26, out27, out28, out29, out30, out31, en
  and and_1 (and_1_out, decoder_1_out0, 1'b0);
  and and_2 (and_2_out, RegWEn, decoder_1_out1);
  and and_3 (and_3_out, RegWEn, decoder_1_out2);
  and and_4 (and_4_out, RegWEn, decoder_1_out5);
  and and_5 (and_5_out, RegWEn, decoder_1_out6);
  and and_6 (and_6_out, RegWEn, decoder_1_out7);
  and and_7 (and_7_out, RegWEn, decoder_1_out8);
  and and_8 (and_8_out, RegWEn, decoder_1_out9);
  and and_9 (and_9_out, RegWEn, decoder_1_out10);
  regfilesadness regfilesadness_1 (
    .clk(clk), .WE(and_1_out), .data(Write_Data), .out_5(regfilesadness_1_out_5));  // open: reset
  regfilesadness regfilesadness_2 (.clk(clk), .WE(and_2_out), .data(Write_Data), .out_5(ra));  // open: reset
  regfilesadness regfilesadness_3 (.clk(clk), .WE(and_3_out), .data(Write_Data), .out_5(sp));  // open: reset
  regfilesadness regfilesadness_4 (.clk(clk), .WE(and_4_out), .data(Write_Data), .out_5(t0));  // open: reset
  regfilesadness regfilesadness_5 (.clk(clk), .WE(and_5_out), .data(Write_Data), .out_5(t1));  // open: reset
  regfilesadness regfilesadness_6 (.clk(clk), .WE(and_6_out), .data(Write_Data), .out_5(t2));  // open: reset
  regfilesadness regfilesadness_7 (.clk(clk), .WE(and_7_out), .data(Write_Data), .out_5(s0));  // open: reset
  regfilesadness regfilesadness_8 (.clk(clk), .WE(and_8_out), .data(Write_Data), .out_5(s1));  // open: reset
  regfilesadness regfilesadness_9 (.clk(clk), .WE(and_9_out), .data(Write_Data), .out_5(a0));  // open: reset
  Multiplexer #(.select(5), .width(32), .enable("false")) multiplexer_1 (
    .in0(regfilesadness_1_out_5), .in1(ra), .in2(sp), .in5(t0), .in6(t1), .in7(t2), .in8(s0), .in9(s1),
    .in10(a0), .out(Read_Data_1), .sel(rs1));  // open: in3, in4, in11, in12, in13, in14, in15, in16, in17, in18, in19, in20, in21, in22, in23, in24, in25, in26, in27, in28, in29, in30, in31
  Multiplexer #(.select(5), .width(32), .enable("false")) multiplexer_2 (
    .in0(regfilesadness_1_out_5), .in1(ra), .in2(sp), .in5(t0), .in6(t1), .in7(t2), .in8(s0), .in9(s1),
    .in10(a0), .out(Read_Data_2), .sel(rs2));  // open: in3, in4, in11, in12, in13, in14, in15, in16, in17, in18, in19, in20, in21, in22, in23, in24, in25, in26, in27, in28, in29, in30, in31

  // Other names for the same wires on the sheet: read_data1[31:0] = Read_Data_1; read_data2[31:0] = Read_Data_2;
  //   read_reg1[4:0] = rs1; read_reg2[4:0] = rs2; write_en = RegWEn; write_reg[4:0] = rd

  // Notes on the sheet:
  //   INPUTS to your circuit
  //   DON'T CHANGE THE LOCATIONS OF THE INPUTS AND OUTPUTS!
  //   These are DEBUG/TEST outputs from your circuit.
  //   OUTPUTS from your circuit
endmodule

module regfilesadness (
  input  reset,
  input  clk,
  input  WE,
  input  [31:0] data,
  output [31:0] out_5
);

  wire in_put;

  and and_1 (in_put, clk, WE);
  D_Flip_Flop d_ff_1 (.D(data[0]), .clk(in_put), .Q(out_5[0]), .reset(reset));  // open: Qn, preset
  D_Flip_Flop d_ff_2 (.D(data[1]), .clk(in_put), .Q(out_5[1]), .reset(reset));  // open: Qn, preset
  D_Flip_Flop d_ff_3 (.D(data[2]), .clk(in_put), .Q(out_5[2]), .reset(reset));  // open: Qn, preset
  D_Flip_Flop d_ff_4 (.D(data[3]), .clk(in_put), .Q(out_5[3]), .reset(reset));  // open: Qn, preset
  D_Flip_Flop d_ff_5 (.D(data[4]), .clk(in_put), .Q(out_5[4]), .reset(reset));  // open: Qn, preset
  D_Flip_Flop d_ff_6 (.D(data[5]), .clk(in_put), .Q(out_5[5]), .reset(reset));  // open: Qn, preset
  D_Flip_Flop d_ff_7 (.D(data[6]), .clk(in_put), .Q(out_5[6]), .reset(reset));  // open: Qn, preset
  D_Flip_Flop d_ff_8 (.D(data[7]), .clk(in_put), .Q(out_5[7]), .reset(reset));  // open: Qn, preset
  D_Flip_Flop d_ff_9 (.D(data[9]), .clk(in_put), .Q(out_5[9]), .reset(reset));  // open: Qn, preset
  D_Flip_Flop d_ff_10 (.D(data[8]), .clk(in_put), .Q(out_5[8]), .reset(reset));  // open: Qn, preset
  D_Flip_Flop d_ff_11 (.D(data[10]), .clk(in_put), .Q(out_5[10]), .reset(reset));  // open: Qn, preset
  D_Flip_Flop d_ff_12 (.D(data[11]), .clk(in_put), .Q(out_5[11]), .reset(reset));  // open: Qn, preset
  D_Flip_Flop d_ff_13 (.D(data[12]), .clk(in_put), .Q(out_5[12]), .reset(reset));  // open: Qn, preset
  D_Flip_Flop d_ff_14 (.D(data[13]), .clk(in_put), .Q(out_5[13]), .reset(reset));  // open: Qn, preset
  D_Flip_Flop d_ff_15 (.D(data[14]), .clk(in_put), .Q(out_5[14]), .reset(reset));  // open: Qn, preset
  D_Flip_Flop d_ff_16 (.D(data[15]), .clk(in_put), .Q(out_5[15]), .reset(reset));  // open: Qn, preset
  D_Flip_Flop d_ff_17 (.D(data[16]), .clk(in_put), .Q(out_5[16]), .reset(reset));  // open: Qn, preset
  D_Flip_Flop d_ff_18 (.D(data[17]), .clk(in_put), .Q(out_5[17]), .reset(reset));  // open: Qn, preset
  D_Flip_Flop d_ff_19 (.D(data[18]), .clk(in_put), .Q(out_5[18]), .reset(reset));  // open: Qn, preset
  D_Flip_Flop d_ff_20 (.D(data[19]), .clk(in_put), .Q(out_5[19]), .reset(reset));  // open: Qn, preset
  D_Flip_Flop d_ff_21 (.D(data[20]), .clk(in_put), .Q(out_5[20]), .reset(reset));  // open: Qn, preset
  D_Flip_Flop d_ff_22 (.D(data[21]), .clk(in_put), .Q(out_5[21]), .reset(reset));  // open: Qn, preset
  D_Flip_Flop d_ff_23 (.D(data[22]), .clk(in_put), .Q(out_5[22]), .reset(reset));  // open: Qn, preset
  D_Flip_Flop d_ff_24 (.D(data[23]), .clk(in_put), .Q(out_5[23]), .reset(reset));  // open: Qn, preset
  D_Flip_Flop d_ff_25 (.D(data[25]), .clk(in_put), .Q(out_5[25]), .reset(reset));  // open: Qn, preset
  D_Flip_Flop d_ff_26 (.D(data[24]), .clk(in_put), .Q(out_5[24]), .reset(reset));  // open: Qn, preset
  D_Flip_Flop d_ff_27 (.D(data[26]), .clk(in_put), .Q(out_5[26]), .reset(reset));  // open: Qn, preset
  D_Flip_Flop d_ff_28 (.D(data[27]), .clk(in_put), .Q(out_5[27]), .reset(reset));  // open: Qn, preset
  D_Flip_Flop d_ff_29 (.D(data[28]), .clk(in_put), .Q(out_5[28]), .reset(reset));  // open: Qn, preset
  D_Flip_Flop d_ff_30 (.D(data[29]), .clk(in_put), .Q(out_5[29]), .reset(reset));  // open: Qn, preset
  D_Flip_Flop d_ff_31 (.D(data[30]), .clk(in_put), .Q(out_5[30]), .reset(reset));  // open: Qn, preset
  D_Flip_Flop d_ff_32 (.D(data[31]), .clk(in_put), .Q(out_5[31]), .reset(reset));  // open: Qn, preset

  // Other names for the same wires on the sheet: in0 = data[0]; in1 = data[1]; in2 = data[2]; in3 = data[3];
  //   in4 = data[4]; in5 = data[5]; in6 = data[6]; in7 = data[7]; in8 = data[8]; in9 = data[9]; in10 = data[10];
  //   in11 = data[11]; in12 = data[12]; in13 = data[13]; in14 = data[14]; in15 = data[15]; in16 = data[16];
  //   in17 = data[17]; in18 = data[18]; in19 = data[19]; in20 = data[20]; in21 = data[21]; in22 = data[22];
  //   in23 = data[23]; in24 = data[24]; in25 = data[25]; in26 = data[26]; in27 = data[27]; in28 = data[28];
  //   in29 = data[29]; in30 = data[30]; in31 = data[31]; out0 = out_5[0]; out1 = out_5[1]; out2 = out_5[2];
  //   out3 = out_5[3]; out4 = out_5[4]; out5 = out_5[5]; out6 = out_5[6]; out7 = out_5[7]; out8 = out_5[8];
  //   out9 = out_5[9]; out10 = out_5[10]; out11 = out_5[11]; out12 = out_5[12]; out13 = out_5[13]; out14 = out_5[14];
  //   out15 = out_5[15]; out16 = out_5[16]; out17 = out_5[17]; out18 = out_5[18]; out19 = out_5[19];
  //   out20 = out_5[20]; out21 = out_5[21]; out22 = out_5[22]; out23 = out_5[23]; out24 = out_5[24];
  //   out25 = out_5[25]; out26 = out_5[26]; out27 = out_5[27]; out28 = out_5[28]; out29 = out_5[29];
  //   out30 = out_5[30]; out31 = out_5[31]

  // Notes on the sheet:
  //   reset
  //   clk
  //   WE
  //   data
endmodule

module fallingsadness (
  input  reset,
  input  clk,
  input  WE,
  input  [31:0] data,
  output [31:0] out_5
);

  wire in_put;

  and and_1 (in_put, clk, WE);
  D_Flip_Flop #(.trigger("falling")) d_ff_1 (
    .D(data[0]), .clk(in_put), .Q(out_5[0]), .reset(reset));  // open: Qn, preset
  D_Flip_Flop #(.trigger("falling")) d_ff_2 (
    .D(data[1]), .clk(in_put), .Q(out_5[1]), .reset(reset));  // open: Qn, preset
  D_Flip_Flop #(.trigger("falling")) d_ff_3 (
    .D(data[2]), .clk(in_put), .Q(out_5[2]), .reset(reset));  // open: Qn, preset
  D_Flip_Flop #(.trigger("falling")) d_ff_4 (
    .D(data[3]), .clk(in_put), .Q(out_5[3]), .reset(reset));  // open: Qn, preset
  D_Flip_Flop #(.trigger("falling")) d_ff_5 (
    .D(data[4]), .clk(in_put), .Q(out_5[4]), .reset(reset));  // open: Qn, preset
  D_Flip_Flop #(.trigger("falling")) d_ff_6 (
    .D(data[5]), .clk(in_put), .Q(out_5[5]), .reset(reset));  // open: Qn, preset
  D_Flip_Flop #(.trigger("falling")) d_ff_7 (
    .D(data[6]), .clk(in_put), .Q(out_5[6]), .reset(reset));  // open: Qn, preset
  D_Flip_Flop #(.trigger("falling")) d_ff_8 (
    .D(data[7]), .clk(in_put), .Q(out_5[7]), .reset(reset));  // open: Qn, preset
  D_Flip_Flop #(.trigger("falling")) d_ff_9 (
    .D(data[9]), .clk(in_put), .Q(out_5[9]), .reset(reset));  // open: Qn, preset
  D_Flip_Flop #(.trigger("falling")) d_ff_10 (
    .D(data[8]), .clk(in_put), .Q(out_5[8]), .reset(reset));  // open: Qn, preset
  D_Flip_Flop #(.trigger("falling")) d_ff_11 (
    .D(data[10]), .clk(in_put), .Q(out_5[10]), .reset(reset));  // open: Qn, preset
  D_Flip_Flop #(.trigger("falling")) d_ff_12 (
    .D(data[11]), .clk(in_put), .Q(out_5[11]), .reset(reset));  // open: Qn, preset
  D_Flip_Flop #(.trigger("falling")) d_ff_13 (
    .D(data[12]), .clk(in_put), .Q(out_5[12]), .reset(reset));  // open: Qn, preset
  D_Flip_Flop #(.trigger("falling")) d_ff_14 (
    .D(data[13]), .clk(in_put), .Q(out_5[13]), .reset(reset));  // open: Qn, preset
  D_Flip_Flop #(.trigger("falling")) d_ff_15 (
    .D(data[14]), .clk(in_put), .Q(out_5[14]), .reset(reset));  // open: Qn, preset
  D_Flip_Flop #(.trigger("falling")) d_ff_16 (
    .D(data[15]), .clk(in_put), .Q(out_5[15]), .reset(reset));  // open: Qn, preset
  D_Flip_Flop #(.trigger("falling")) d_ff_17 (
    .D(data[16]), .clk(in_put), .Q(out_5[16]), .reset(reset));  // open: Qn, preset
  D_Flip_Flop #(.trigger("falling")) d_ff_18 (
    .D(data[17]), .clk(in_put), .Q(out_5[17]), .reset(reset));  // open: Qn, preset
  D_Flip_Flop #(.trigger("falling")) d_ff_19 (
    .D(data[18]), .clk(in_put), .Q(out_5[18]), .reset(reset));  // open: Qn, preset
  D_Flip_Flop #(.trigger("falling")) d_ff_20 (
    .D(data[19]), .clk(in_put), .Q(out_5[19]), .reset(reset));  // open: Qn, preset
  D_Flip_Flop #(.trigger("falling")) d_ff_21 (
    .D(data[20]), .clk(in_put), .Q(out_5[20]), .reset(reset));  // open: Qn, preset
  D_Flip_Flop #(.trigger("falling")) d_ff_22 (
    .D(data[21]), .clk(in_put), .Q(out_5[21]), .reset(reset));  // open: Qn, preset
  D_Flip_Flop #(.trigger("falling")) d_ff_23 (
    .D(data[22]), .clk(in_put), .Q(out_5[22]), .reset(reset));  // open: Qn, preset
  D_Flip_Flop #(.trigger("falling")) d_ff_24 (
    .D(data[23]), .clk(in_put), .Q(out_5[23]), .reset(reset));  // open: Qn, preset
  D_Flip_Flop #(.trigger("falling")) d_ff_25 (
    .D(data[25]), .clk(in_put), .Q(out_5[25]), .reset(reset));  // open: Qn, preset
  D_Flip_Flop #(.trigger("falling")) d_ff_26 (
    .D(data[24]), .clk(in_put), .Q(out_5[24]), .reset(reset));  // open: Qn, preset
  D_Flip_Flop #(.trigger("falling")) d_ff_27 (
    .D(data[26]), .clk(in_put), .Q(out_5[26]), .reset(reset));  // open: Qn, preset
  D_Flip_Flop #(.trigger("falling")) d_ff_28 (
    .D(data[27]), .clk(in_put), .Q(out_5[27]), .reset(reset));  // open: Qn, preset
  D_Flip_Flop #(.trigger("falling")) d_ff_29 (
    .D(data[28]), .clk(in_put), .Q(out_5[28]), .reset(reset));  // open: Qn, preset
  D_Flip_Flop #(.trigger("falling")) d_ff_30 (
    .D(data[29]), .clk(in_put), .Q(out_5[29]), .reset(reset));  // open: Qn, preset
  D_Flip_Flop #(.trigger("falling")) d_ff_31 (
    .D(data[30]), .clk(in_put), .Q(out_5[30]), .reset(reset));  // open: Qn, preset
  D_Flip_Flop #(.trigger("falling")) d_ff_32 (
    .D(data[31]), .clk(in_put), .Q(out_5[31]), .reset(reset));  // open: Qn, preset

  // Other names for the same wires on the sheet: in0 = data[0]; in1 = data[1]; in2 = data[2]; in3 = data[3];
  //   in4 = data[4]; in5 = data[5]; in6 = data[6]; in7 = data[7]; in8 = data[8]; in9 = data[9]; in10 = data[10];
  //   in11 = data[11]; in12 = data[12]; in13 = data[13]; in14 = data[14]; in15 = data[15]; in16 = data[16];
  //   in17 = data[17]; in18 = data[18]; in19 = data[19]; in20 = data[20]; in21 = data[21]; in22 = data[22];
  //   in23 = data[23]; in24 = data[24]; in25 = data[25]; in26 = data[26]; in27 = data[27]; in28 = data[28];
  //   in29 = data[29]; in30 = data[30]; in31 = data[31]; out0 = out_5[0]; out1 = out_5[1]; out2 = out_5[2];
  //   out3 = out_5[3]; out4 = out_5[4]; out5 = out_5[5]; out6 = out_5[6]; out7 = out_5[7]; out8 = out_5[8];
  //   out9 = out_5[9]; out10 = out_5[10]; out11 = out_5[11]; out12 = out_5[12]; out13 = out_5[13]; out14 = out_5[14];
  //   out15 = out_5[15]; out16 = out_5[16]; out17 = out_5[17]; out18 = out_5[18]; out19 = out_5[19];
  //   out20 = out_5[20]; out21 = out_5[21]; out22 = out_5[22]; out23 = out_5[23]; out24 = out_5[24];
  //   out25 = out_5[25]; out26 = out_5[26]; out27 = out_5[27]; out28 = out_5[28]; out29 = out_5[29];
  //   out30 = out_5[30]; out31 = out_5[31]

  // Notes on the sheet:
  //   reset
  //   clk
  //   WE
  //   data
endmodule
